# Fritzing sketch non-contact water detect (saved by Fritzing 0.9.3b)
circuit board: 6cm x 5.5cm

parts:
  ESP-32 = DOIT Esp32 DevKit v1 (30 pins long, 11 pins width) [part_number=ESP32S-PIN30]
  Water_sensor = male pin header, 4 pins [form="♂ (male)"]
  buttom = Header 2 [package=r_sw_th]
  Buzzer = Buzzer 12mm [package=buzzer-12mm-ns-kit]

nets:
  N1: ESP-32.GND, Water_sensor.pin3, buttom.2
  N2: ESP-32.D2, Buzzer.1
  N3: ESP-32.D26, Water_sensor.pin4
  N4: ESP-32.VIN, Water_sensor.pin1, Water_sensor.pin2
  N5: buttom.1, Buzzer.2

custom parts:
  DOIT Esp32 DevKit v1 (30 pins long, 11 pins width): The DOIT Esp32 DevKit v1 is one of the development board created by DOIT to evaluate the ESP-WROOM-32 module. It is based on the ESP32 microcontroller that boasts Wifi, Bluetooth, Ethernet and Low Power support all in a single chip. (vanepp) made breadboard work, adjusted pin numbering and labels and reduced size of schematic and cleaned up pcb. This chip is 30pins long (2 x15) and 11 pins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
